// Digital circuit huseyinalper_enismert_eggtimer.dig as structural Verilog
module huseyinalper_enismert_eggtimer (
  input  _1_kHz
);

  wire PRESET_out, RST_out, START_out, u_controller_countdown, u_controller_load, u_controller_start,
       u_counter_endd, u_downcounter_zero;
  wire [3:0] dipswitch_1_out, dipswitch_5_out, dipswitch_9_out, dipswitch_13_out, u_downcounter_m1,
       u_downcounter_m10, u_downcounter_s1, u_downcounter_s10;

  Button #(.activeLow("true")) RST (.out(RST_out));
  Seven_Seg_Hex seven_seg_hex_1 (.d(u_downcounter_m10), .dp(1'b0));
  DipSwitch dipswitch_1 (.out(dipswitch_1_out[3]));
  DipSwitch dipswitch_2 (.out(dipswitch_1_out[2]));
  DipSwitch dipswitch_3 (.out(dipswitch_1_out[1]));
  Seven_Seg_Hex seven_seg_hex_2 (.d(u_downcounter_m1), .dp(1'b1));
  downcounter #(.applicationType("IVERILOG")) u_downcounter (
    .rst(RST_out), .c1khz(_1_kHz), .count(u_controller_countdown), .load(u_controller_load),
    .pm10(dipswitch_1_out), .pm1(dipswitch_5_out), .ps10(dipswitch_9_out), .ps1(dipswitch_13_out),
    .m10(u_downcounter_m10), .m1(u_downcounter_m1), .s10(u_downcounter_s10), .s1(u_downcounter_s1),
    .zero(u_downcounter_zero));
  DipSwitch dipswitch_4 (.out(dipswitch_1_out[0]));
  DipSwitch dipswitch_5 (.out(dipswitch_5_out[3]));
  DipSwitch dipswitch_6 (.out(dipswitch_5_out[2]));
  Seven_Seg_Hex seven_seg_hex_3 (.d(u_downcounter_s10), .dp(1'b0));
  DipSwitch dipswitch_7 (.out(dipswitch_5_out[1]));
  DipSwitch dipswitch_8 (.out(dipswitch_5_out[0]));
  DipSwitch dipswitch_9 (.out(dipswitch_9_out[3]));
  Seven_Seg_Hex seven_seg_hex_4 (.d(u_downcounter_s1), .dp(1'b0));
  DipSwitch dipswitch_10 (.out(dipswitch_9_out[2]));
  DipSwitch dipswitch_11 (.out(dipswitch_9_out[1]));
  DipSwitch dipswitch_12 (.out(dipswitch_9_out[0]));
  DipSwitch dipswitch_13 (.out(dipswitch_13_out[3]));
  DipSwitch dipswitch_14 (.out(dipswitch_13_out[2]));
  DipSwitch dipswitch_15 (.out(dipswitch_13_out[1]));
  DipSwitch dipswitch_16 (.out(dipswitch_13_out[0]));
  controller #(.applicationType("IVERILOG")) u_controller (
    .clk(_1_kHz), .rst(RST_out), .beginn(START_out), .reset(PRESET_out), .zero(u_downcounter_zero),
    .endd(u_counter_endd), .load(u_controller_load), .start(u_controller_start),
    .countdown(u_controller_countdown));
  Button START (.out(START_out));
  Button PRESET (.out(PRESET_out));
  counter #(.applicationType("IVERILOG")) u_counter (
    .rst(RST_out), .clk(_1_kHz), .start(u_controller_start), .endd(u_counter_endd));

  // Notes on the sheet:
  //   _1_kHz: Hz: 1000
endmodule

/* Code of downcounter:
module downcounter(
    input rst, c1khz,
    input count, load, 
    input [3:0] pm10,
    input [3:0] pm1,
    input [3:0] ps10,
    input [3:0] ps1,
    output reg [3:0] m10,
    output reg [3:0] m1,
    output reg [3:0] s10,
    output reg [3:0] s1,
    output zero
    );

    reg [3:0] display1;
    reg [3:0] display2;
    reg [3:0] display3;
    reg [3:0] display4;

    reg hitZero;

    assign zero = (hitZero == 1);

    always @(posedge c1khz, negedge rst)
    begin
        if (rst == 0) // resets everything
            begin
                display1 <= 0;
                display2 <= 0;
                display3 <= 0;
                display4 <= 0;
            end
        else if (load == 1) // loads up to 99:59
            begin
		if (pm10 > 9)
			begin
				display1 <= 9;
			end
		else
			begin
				display1 <= pm10;	
			end
		if (pm1 > 9)
			begin
				display2 <= 9;
			end
		else
			begin
				display2<= pm1;	
			end
		if (ps10 > 5)
			begin
				display3 <= 5;
			end
		else
			begin
				display3 <= ps10;	
			end
		if (ps1 > 9)
			begin
				display4 <= 9;
			end
		else
			begin
				display4 <= ps1;	
			end
                hitZero <= 0;
            end
        else if (count == 1) // counts down
            begin
                if (display4 != 0)
                    begin
                        display4 <= display4 - 1;
                        hitZero <= 0;
                    end
                else
                    begin
                        if (display3 != 0)
                            begin
                                display3 <= display3 - 1;
                                display4 <= 9;
                                hitZero <= 0;
                            end
                        else
                            begin
                                if (display2 != 0)
                                    begin
                                        display2 <= display2 - 1;
                                        display3 <= 5;
                                        display4 <= 9;
                                        hitZero <= 0;
                                    end
                                else
                                    begin
                                        if (display1 != 0)
                                            begin
                                                display1 <= display1 - 1;
                                                display2 <= 9;
                                                display3 <= 5;
                                                display4 <= 9;
                                                hitZero <= 0;
                                            end
                                        else
                                            begin
                                                hitZero <= 1;
                                            end
                                    end
                            end
                    end
            end
        m10 <= display1;
        m1 <= display2;
        s10 <= display3;
        s1 <= display4;
    end // always
endmodule
*/

/* Code of controller:
module controller(
    input clk,
    input rst,
    input beginn, 
    input reset,
    input zero,
    input endd,
    output load,
    output start,
    output countdown
    );

    reg loadReg = 0;
    reg startReg = 0;
    reg countDownReg = 0;
    reg countingReg = 0; // checks if it continues to count
    reg [1:0] state; // stores the state (00, 01, 10)
    
    localparam [1:0]
	stateCountDown = 2'b00,
	stateStart = 2'b01,
	statePreset = 2'b10;

    assign load = (loadReg == 1);
    assign start = (startReg == 1);
    assign countdown = (countDownReg == 1);

    always @(posedge clk)
    begin
	loadReg <= 0;
	startReg <= 0;
	countDownReg <= 0;
	if (~reset && ~beginn) // 00
	    begin
		state <= stateCountDown;
	    end
	else if (~reset && beginn) // 01
	    begin
		state <= stateStart;
	    end
	else if (reset && ~beginn) // 10
	    begin
		state <= statePreset;
	    end
    end // always

    always @(negedge rst)
    begin
	loadReg <= 0;
	startReg <= 0;
	countDownReg <= 0;
	if (~reset && ~beginn) // 00
	    begin
		state <= stateCountDown;
	    end
	else if (~reset && beginn) // 01
	    begin
		state <= stateStart;
	    end
	else if (reset && ~beginn) // 10
	    begin
		state <= statePreset;
	    end
    end // always

    always @(state)
    begin
	case(state)
	    statePreset:
	        begin
		    loadReg <= 1;
		    countingReg <= 0; // stops counting
	        end
	    stateStart:
	        begin
		    startReg <= 1;
		    countingReg <= 1; // starts counting
	        end
	    stateCountDown: // counts down
	        begin
		    if (endd && countingReg)
			begin
			    startReg <= 1;
			    countDownReg <= 1;
			end
	        end
	endcase
    end // always

    always @(endd)
    begin
	if (endd && countingReg)
	    begin
		startReg <= 1;
		countDownReg <= 1;
	    end
    end
endmodule
*/

/* Code of counter:
module counter(
    input rst,
    input clk,
    input start,
    output endd);
    
    reg [9:0] cnt;
    
    assign endd = (cnt == 0);
    
    always @(posedge clk, negedge rst)
    begin
        if (~rst)
        begin
            cnt <= 0;
        end
        else
        begin
            if (start)
                cnt <= 999;
            else if (~endd)
                cnt <= cnt-1;
        end
    end //always
endmodule
*/
